# Fritzing sketch Remote control simulation (saved by Fritzing 1.0.6)
breadboards: 2

parts:
  Mod1 = KY-033 Line Tracking Sensor Module [package="Breakout board"]
  D1 = LTE-302 [package=lte-302]
  S1 = Pushbutton [package="[THT]"]
  S2 = Pushbutton [package="[THT]"]
  S3 = Pushbutton [package="[THT]"]
  R1 = Resistor [tolerance=±5% resistance=220 package="2010 [SMD]"]
  R2 = Resistor [tolerance=±5% resistance=220 package="2010 [SMD]"]
  R3 = Resistor [tolerance=±5% resistance=220 package="2010 [SMD]"]
  R4 = Resistor [tolerance=±5% resistance=220 package="2010 [SMD]"]
  R5 = Resistor [tolerance=±5% resistance=220 package="2010 [SMD]"]
  R6 = Resistor [tolerance=±5% resistance=220 package="2010 [SMD]"]
  R7 = Resistor [tolerance=±5% resistance=220 package="2010 [SMD]"]
  LED1 = RGB LED - (4 legs) [color="Red (633nm)" current=0.030A package="5 mm [THT]"]
  Part1 = Arduino Uno (Rev3)
  Part2 = Arduino Uno (Rev3)

nets:
  GND: Mod1.GND, LED1.common_anode, Part1.GND
  N1: Mod1.OUT, Part1.D3_PWM
  VCC: Mod1.VCC, Part1.5V
  N2: D1.A, R4.Pin_0
  N3: D1.C, R5.Pin_0, R6.Pin_0, R7.Pin_0, Part2.GND
  N4: S1.Pin_1, S1.Pin_2, S2.Pin_1, S2.Pin_2, S3.Pin_1, S3.Pin_2, Part2.5V
  N5: S1.Pin_3, S1.Pin_4, R7.Pin_1, Part2.D4
  N6: S2.Pin_3, S2.Pin_4, R5.Pin_1, Part2.D6_PWM
  N7: S3.Pin_3, S3.Pin_4, R6.Pin_1, Part2.D5_PWM
  N8: R1.Pin_0, Part1.D6_PWM
  N9: R1.Pin_1, LED1.blue_cathode
  N10: R2.Pin_0, Part1.D5_PWM
  N11: R2.Pin_1, LED1.green_cathode
  N12: R3.Pin_0, Part1.D4
  N13: R3.Pin_1, LED1.red_cathode
  N14: R4.Pin_1, Part2.D3_PWM

custom parts:
  KY-033 Line Tracking Sensor Module: KY-033 line tracking sensor module. An infrared sensor used to detect opaque surfaces.
